# Fritzing sketch Untitled Sketch (saved by Fritzing 0.7.12b)
breadboards: 1

parts:
  U1 = atmega168 [package=dip]  # not connected
  U3 = atmega168 smd [package=tqfp]  # not connected
  VREG1 = KA78R05 Low Dropout Voltage Regulator [part_number=KA78R05 package=TO-220F-4L]  # not connected
  C1 = Ceramic Capacitor [package=THT]  # not connected
  U5 = Voltage Regulator - 5V [package="TO220 [THT]"]
  C2 = Ceramic Capacitor [capacitance=100nF package="100 mil [THT, multilayer]"]  # not connected
  J1 = double row female pin header, 10 pins [form="♀ (female)"]
  C3 = Ceramic Capacitor [capacitance=100nF package="100 mil [THT, multilayer]"]

nets:
  N1: U5.input_voltage, C3.0
  N2: J1.pin10, C3.1
