# Fritzing sketch DaliShield (saved by Fritzing 0.7.12b)
breadboards: 2

parts:
  Arduino1 = Arduino  # not connected
  DALI = screw terminal, 2 pins
  DF10S-E3/77_-_DFS-WRONG = IC, DIP package, 4 pins [chip_label=IC]
  U1 = Optocoupler [package=THT]  # not connected

nets:
  N1: DALI.pin1, DF10S-E3/77_-_DFS-WRONG.pin3
  N2: DALI.pin2, DF10S-E3/77_-_DFS-WRONG.pin4

notes:
  12-24VDC +
  12-24VDC -
  DALI Shield
  V1.0 2013-05-06
