# Fritzing sketch Pixelcontroller1-alles (saved by Fritzing 0.7.12b)
breadboards: 2

parts:
  C4 = Ceramic Capacitor [capacitance=100nF voltage=35V package="100 mil [THT, multilayer]"]
  Q2 = Basic FET N-Channel [part_number=IRLIZ44N package="TO220 [THT]"]
  Q3 = Basic FET N-Channel [part_number=IRLZ34N package="TO220 [THT]"]
  Q4 = Basic FET N-Channel [part_number=IRLIZ44N package="TO220 [THT]"]
  S3 = Pushbutton [package=THT]
  J1 = Screw terminal - 2 pins [package=THT]
  IC1 = IC, DIP package, 8 pins [chip_label=TC427 part_number=TC427]
  Q4_2 = Basic FET N-Channel [part_number=IRLIZ44N package="TO220 [THT]"]
  J2 = Screw terminal - 2 pins [package=THT]
  IC1_2 = IC, DIP package, 8 pins [chip_label=TC427 part_number=TC427]
  J1_2 = Screw terminal - 2 pins [package=THT]
  R1 = Resistor [tolerance=±5% resistance=10k package=THT]
  R2 = Resistor [tolerance=±5% resistance=10k package=THT]
  R3 = Resistor [tolerance=±5% resistance=10k package=THT]
  R4 = Resistor [tolerance=±5% resistance=10k package=THT]
  R9 = Resistor [tolerance=±5% resistance=4.7k package=THT]
  S4 = Pushbutton [package=THT]
  R10 = Resistor [tolerance=±5% resistance=4.7k package=THT]
  J4 = Screw terminal - 2 pins [package=THT]
  J3 = Screw terminal - 2 pins [package=THT]
  R11 = Resistor [tolerance=±5% resistance=1.5k package=THT]
  LED5 = LED - 3mm [color="Yellow (595nm)" current=2mA package="3 mm [THT]"]
  Arduino1 = Arduino
  C3 = Electrolytic Capacitor [capacitance=0.22mF voltage=35V package="100 mil [THT, electrolytic]"]
  C2 = Ceramic Capacitor [capacitance=100nF voltage=35V package="100 mil [THT, multilayer]"]
  C1 = Ceramic Capacitor [capacitance=100nF voltage=35V package="100 mil [THT, multilayer]"]
  DS18B20 = NPN-Transistor [part_number=DS18B20 package="TO92 [THT]"]
  J6 = Screw terminal - 2 pins [package=THT]

nets:
  N1: C4.0, S3.leg1
  N2: C4.1, Arduino1.RST
  N3: Q2.gate, IC1_2.pin7
  N4: Q2.drain, J1_2.pin1
  N5: Q2.source, Q3.source, Q4.source, S3.leg0, IC1.pin3, Q4_2.source, IC1_2.pin3, R1.Pin_1, R2.Pin_1, R3.Pin_1, R4.Pin_1, S4.leg1, J3.pin1, J3.pin2, LED5.cathode, Arduino1.GND, C3.-, C2.0, C1.0, DS18B20.E, DS18B20.C, J6.pin2
  N6: Q3.gate, IC1.pin5
  N7: Q3.drain, J2.pin2
  N8: Q4.gate, IC1_2.pin5
  N9: Q4.drain, J1_2.pin2
  N10: J1.pin1, Arduino1.D13
  N11: J1.pin2, Arduino1.D11
  N12: IC1.pin2, R1.Pin_0, Arduino1.D10
  N13: IC1.pin4, R2.Pin_0, Arduino1.D9
  N14: IC1.pin6, IC1_2.pin6, R9.Pin_0, R10.Pin_0, Arduino1.+5V, C3.+, C2.1, C1.1
  N15: IC1.pin7, Q4_2.gate
  N16: Q4_2.drain, J2.pin1
  N17: IC1_2.pin2, R4.Pin_0, Arduino1.D6
  N18: IC1_2.pin4, R3.Pin_0, Arduino1.D3
  N19: R9.Pin_1, Arduino1.D7, DS18B20.B, J6.pin1
  N20: S4.leg0, R10.Pin_1, Arduino1.D2
  N21: J4.pin1, J4.pin2
  N22: R11.Pin_0, Arduino1.D8
  N23: R11.Pin_1, LED5.anode

notes:
  12-24VDC +
  12-24VDC -
