# Fritzing sketch Pixelcontroller1 (saved by Fritzing 0.7.12b)
breadboards: 2

parts:
  C4 = Ceramic Capacitor [capacitance=100nF voltage=35V package="100 mil [THT, multilayer]"]
  Q2 = Basic FET N-Channel [part_number=IRLIZ44N package="TO220 [THT]"]
  Q3 = Basic FET N-Channel [part_number=IRLZ34N package="TO220 [THT]"]
  Q4 = Basic FET N-Channel [part_number=IRLIZ44N package="TO220 [THT]"]
  S3 = Pushbutton [package=THT]
  Pixel = Screw terminal - 2 pins [package=THT]
  Q4_2 = Basic FET N-Channel [part_number=IRLIZ44N package="TO220 [THT]"]
  J2_B-_W- = Screw terminal - 2 pins [package=THT]
  J1_R-_G- = Screw terminal - 2 pins [package=THT]
  R1 = Resistor [tolerance=±5% resistance=10k package=THT]
  R2 = Resistor [tolerance=±5% resistance=10k package=THT]
  R3 = Resistor [tolerance=±5% resistance=10k package=THT]
  R4 = Resistor [tolerance=±5% resistance=10k package=THT]
  S4 = Pushbutton [package=THT]
  12V_in = Screw terminal - 2 pins [package=THT]
  12V- = Screw terminal - 2 pins [package=THT]
  R11 = Resistor [tolerance=±5% resistance=1.5k package=THT]
  LED5 = LED - 3mm [color="Yellow (595nm)" current=2mA package="3 mm [THT]"]
  Arduino1 = Arduino
  C3 = Electrolytic Capacitor [capacitance=0.22mF voltage=35V package="100 mil [THT, electrolytic]"]
  C2 = Ceramic Capacitor [capacitance=100nF voltage=35V package="100 mil [THT, multilayer]"]
  C1 = Ceramic Capacitor [capacitance=100nF voltage=35V package="100 mil [THT, multilayer]"]
  1-Wire = Screw terminal - 2 pins [package=THT]
  U1 = ICL 7667 [part_number="ICL 7667" package=DIP8]
  U2 = ICL 7667 [part_number="ICL 7667" package=DIP8]
  R12 = Resistor [tolerance=±5% resistance=4.7k package=THT]
  T2 = DS18B20 Temperature Sensor [part_number=DS18B20 package="TO92 [THT]"]  # not connected

nets:
  N1: C4.0, S3.leg1
  N2: C4.1, Arduino1.RST
  N3: Q2.gate, U2.Pin_7
  N4: Q2.drain, J1_R-_G-.pin1
  N5: Q2.source, Q3.source, Q4.source, S3.leg0, Q4_2.source, R1.Pin_1, R2.Pin_1, R3.Pin_1, R4.Pin_1, S4.leg1, 12V-.pin1, 12V-.pin2, LED5.cathode, Arduino1.GND, C3.-, C2.0, C1.0, U1.Pin_3, U2.Pin_3
  N6: Q3.gate, U1.Pin_5
  N7: Q3.drain, J2_B-_W-.pin2
  N8: Q4.gate, U2.Pin_5
  N9: Q4.drain, J1_R-_G-.pin2
  N10: Pixel.pin1, Arduino1.D13
  N11: Pixel.pin2, Arduino1.D11
  N12: Q4_2.gate, U1.Pin_7
  N13: Q4_2.drain, J2_B-_W-.pin1
  N14: R1.Pin_0, Arduino1.D9, U1.Pin_2
  N15: R2.Pin_0, Arduino1.D10, U1.Pin_4
  N16: R3.Pin_0, Arduino1.D6, U2.Pin_4
  N17: R4.Pin_0, Arduino1.D3, U2.Pin_2
  N18: S4.leg0, Arduino1.D2, R12.Pin_1
  N19: 12V_in.pin1, 12V_in.pin2
  N20: R11.Pin_0, Arduino1.D8
  N21: R11.Pin_1, LED5.anode
  N22: Arduino1.D7, 1-Wire.pin1
  N23: Arduino1.+5V, C3.+, C2.1, C1.1, U1.Pin_6, U2.Pin_6, R12.Pin_0

notes:
  12-24VDC +
  12-24VDC -

custom parts:
  ICL 7667: L' ICL7667 est un pilote à grande vitesse monolithique double conçu pour convertir les signaux de niveau TTL en sorties à courant élevé à des tensions allant jusqu'à 15V. Sa haute vitesse et sa sortie courant permettre de piloter de grandes charges capacitives avec des vitesses de balayage élevées et de faibles retards de propagation. Avec une écart de tension de sortie de seulement quelques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
  DS18B20 Temperature Sensor: A DS18B20 temperature sensor with a temperature range from -55 à +125 °C.
