# Fritzing sketch 02_attiny84-base-counter (saved by Fritzing 0.8.3b)
breadboards: 1

parts:
  C1 = Ceramic Capacitor [capacitance=100nF package="100 mil [THT, multilayer]"]
  OW-RX_LED_(optional) = smd LED [color="Blue (525nm)" package="0603 [SMD]"]
  IC1 = DIP - 14 pins [chip_label=ATTiny84 package="DIP (Dual Inline) [THT]"]
  ISP_MISO_Counter4 = female pin header, 1 pin [form="♀ (female)"]
  ISP_SCK_Counter3 = female pin header, 1 pin [form="♀ (female)"]
  ISP_MOSI = female pin header, 1 pin [form="♀ (female)"]
  ISP_RESET = female pin header, 1 pin [form="♀ (female)"]
  ISP_GND = female pin header, 1 pin [form="♀ (female)"]
  ISP_VCC = female pin header, 1 pin [form="♀ (female)"]
  1-Wire_Vcc_Data_GND = screw terminal, 3 pins
  D1 = Rectifier Diode [part_number=1N4148 package="300 mil [THT]"]
  D2 = Rectifier Diode [part_number=1N4148 package="300 mil [THT]"]
  C2 = Electrolytic Capacitor [capacitance=0.47mF package="100 mil [THT, electrolytic]"]
  C3 = Tantalum Capacitor [capacitance="1 μF" package="100 mil [THT, tantalum]"]
  Counter1 = female pin header, 1 pin [form="♀ (female)"]
  R6 = Resistor [tolerance=±5% resistance=100k package=THT]
  R7 = Resistor [tolerance=±5% resistance=10k package=THT]
  Counter2 = female pin header, 1 pin [form="♀ (female)"]
  eHZ_/_SML_RX = female pin header, 1 pin [form="♀ (female)"]
  R8 = Resistor [tolerance=±5% resistance=2.2k package=THT]

nets:
  N1: C1.0, IC1.VCC, ISP_VCC.pin1
  GND: C1.1, OW-RX_LED_(optional).cathode, IC1.GND, ISP_GND.pin1, 1-Wire_Vcc_Data_GND.pin1, C2.-, C3.-, R6.Pin_1
  N2: OW-RX_LED_(optional).anode, R8.Pin_0
  N3: IC1.PB0, D1.cathode, C3.+, R6.Pin_0
  N4: IC1.PB1, Counter1.pin1
  N5: IC1.PB3, ISP_RESET.pin1, R7.Pin_1
  N6: IC1.PB2, 1-Wire_Vcc_Data_GND.pin2
  N7: IC1.PA7, eHZ_/_SML_RX.pin1
  N8: IC1.PA6, ISP_MOSI.pin1
  N9: IC1.PA5, ISP_MISO_Counter4.pin1
  N10: IC1.PA4, ISP_SCK_Counter3.pin1
  N11: IC1.PA3, Counter2.pin1
  N12: IC1.PA2, R8.Pin_1
  VCC 2.8-5V: D1.anode, D2.anode
  N13: D2.cathode, C2.+, R7.Pin_0

notes:
  E1 - Counter 1.01

custom parts:
  DIP - 14 pins: A DIP stand-in part for whatever IC you want. With 14 pins on a 300mil dual inline package (DIP) footprint.
